# Fritzing sketch master (saved by Fritzing 0.9.3b)
circuit board: 8.46667cm x 5.64444cm
breadboards: 1

parts:
  U1 = atmega328 [package=dip]
  RFM1 = RFM69HCW ISM Transciever
  D1 = LTE-302 [package=lte-302]
  D2 = LTE-302 [package=lte-302]
  D3 = LTE-302 [package=lte-302]
  Y1 = CRYSTAL [package=hc49up]
  C1 = Ceramic Capacitor [capacitance=10pF voltage=16V package="0603 [SMD, multilayer]"]
  C2 = Ceramic Capacitor [capacitance="100 nF" package="0603 [SMD, multilayer]"]
  ANT1 = Antenna  # not connected
  S1 = Momentary Switch [package=tactile-pth]
  R1 = Resistor [tolerance=±5% resistance=220 package="1206 [SMD]"]  # not connected
  R2 = Resistor [tolerance=±5% resistance=220 package="1206 [SMD]"]
  R3 = Resistor [tolerance=±5% resistance=220 package="1206 [SMD]"]  # not connected
  R4 = Resistor [tolerance=±5% resistance=220 package="0805 [SMD]"]
  C3 = Electrolytic Capacitor [capacitance=100µF package="200 mil [THT, electrolytic]"]

nets (from the schematic view):
  N1: U1.RESET, S1.4
  N2: U1.D2, RFM1.14_DIO0
  N3: U1.D3_(PWM), U1.A5
  N4: U1.VCC, RFM1.13_3.3V, R4.Pin_1
  N5: U1.GND#7, D1.C, D2.C, D3.C, C1.1, C2.1, S1.3
  N6: U1.XLAT1, Y1.2
  N7: U1.XLAT2, Y1.1, C2.0
  N8: U1.D10_(PWM), RFM1.5_NSS_(CS)
  N9: U1.D11_(PWM), RFM1.3_MOSI
  N10: U1.D12, RFM1.2_MISO
  N11: U1.D13, RFM1.4_SCK
  N12: U1.GND#21, RFM1.1_GND, C3.-
  N13: D2.A, R2.Pin_0

custom parts:
  RFM69HCW ISM Transciever: RF Transceiver by Hope RF. Well supported Arduino libraries are available. This ISM band transceiver is available in several frequencies e.g. 433MHz and 915MHz and it is also available in various feature versions.
